# Fritzing sketch Part4 (saved by Fritzing 0.9.3b)
breadboards: 2

parts:
  R1 = Trimmer Potentiometer [maximum_resistance=10kΩ package=THT]
  LED1 = LED - 5mm [color="Red (633nm)" package="5 mm [THT]"]
  LCD2 = LCD screen
  Part1 = Arduino Uno (Rev3)
  R2 = Resistor [tolerance=±5% resistance=5k package=THT]
  R3 = Resistor [tolerance=±5% resistance=5k package=THT]
  Part3 = Real Time Clock Module - DS1307 RTC Breakout Board
  LED2 = LED - 5mm [color="Red (633nm)" package="5 mm [THT]"]
  R4 = Resistor [tolerance=±5% resistance=5k package=THT]
  Part4 = Barometric Pressure Sensor - BMP085 Breakout

nets:
  5V: R1.leg1, LED1.cathode, LED1.anode, LCD2.VDD, Part1.5V, R2.Pin_0, R3.Pin_0, Part3.5V, R4.Pin_0
  N1: R1.wiper, LCD2.V0
  GND: R1.leg2, LCD2.VSS, LCD2.R/W, LCD2.LED-, Part1.D11_PWM/MOSI, Part1.GND, Part3.GND, Part4.GND
  N2: LCD2.E, Part1.D10_PWM/SS
  N3: LCD2.DB4, Part1.D6_PWM
  N4: LCD2.DB5, Part1.D5_PWM
  N5: LCD2.DB6, Part1.D4
  N6: LCD2.DB7, Part1.D3_PWM
  N7: LCD2.LED+, R3.Pin_1
  N8: Part1.A4/SDA, Part3.SDA, Part4.SDA
  N9: Part1.A5/SCL, Part3.SCL, Part4.SCL
  N10: Part1.D8, R2.Pin_1
  N11: Part1.D7, LED2.cathode, LED2.anode, R4.Pin_1
  3V3: Part1.3V3, Part4.VCC
